# Fritzing sketch mini-weerstation-deel-1 (saved by Fritzing 0.9.3b)
breadboards: 1

parts:
  Part2 = Arduino Uno (Rev3) - ICSP
  RHT1 = Humidity and Temperature Sensor RHT03
  R1 = Resistor [tolerance=±5% resistance=4.7 package=THT]
  LCD2 = LCD screen  # not connected

nets:
  N1: Part2.D12/MISO, RHT1.Data-signal, R1.Pin_0
  5V: Part2.5V, RHT1.Vcc, R1.Pin_1
  N2: Part2.GND, RHT1.GND_2

notes:
  Vcc
  GND
  SCL
  SDA
