# Fritzing sketch mini-weerstation-deel-2 (saved by Fritzing 0.9.3b)
breadboards: 1

parts:
  Part2 = Arduino Uno (Rev3) - ICSP
  RHT1 = Humidity and Temperature Sensor RHT03
  R1 = Resistor [tolerance=±5% resistance=4.7 package=THT]
  LCD2 = LCD screen  # not connected
  R2 = Resistor [tolerance=±5% resistance=100 package=THT]
  DS2 = DS18B20 1-Wire Temperature Sensor [part_number=DS18B20]

nets:
  GND: Part2.GND, RHT1.GND_2, DS2.GND
  N1: Part2.D12/MISO, RHT1.Data-signal, R1.Pin_0
  5V: Part2.5V, RHT1.Vcc, R1.Pin_1, R2.Pin_1, DS2.VDD
  N2: R2.Pin_0, DS2.DQ

notes:
  Vcc
  GND
  SCL
  SDA
