# Fritzing sketch stopwatch (saved by Fritzing 0.9.3b)
breadboards: 1

parts:
  Part2 = Arduino Uno (Rev3) - ICSP
  LCD2 = LCD screen  # not connected
  R1 = Resistor [tolerance=±5% resistance=12k package=THT]
  S1 = Pushbutton [package="[THT]"]
  R2 = Resistor [tolerance=±5% resistance=12k package=THT]
  S2 = Pushbutton [package="[THT]"]

nets:
  N1: Part2.D10_PWM/SS, R2.Pin_0, S2.Pin_1, S2.Pin_2
  N2: Part2.D12/MISO, R1.Pin_0, S1.Pin_1, S1.Pin_2
  N3: Part2.GND, R1.Pin_1, R2.Pin_1
  N4: Part2.5V, S1.Pin_3, S1.Pin_4, S2.Pin_3, S2.Pin_4

notes:
  Vcc
  GND
  SCL
  SDA
